// Digital circuit adders.dig as structural Verilog
module adders (
  input  A,
  input  B,
  input  Cin,
  input  A_2,
  input  B_2,
  input  A_3,
  input  B_3,
  input  Cin_2,
  input  A_4,
  input  B_4,
  input  A_5,
  input  B_5,
  input  A_6,
  input  B_6,
  input  A_7,
  input  B_7,
  input  A_8,
  input  B_8,
  output S,
  output Cout,
  output S_2,
  output Cout_2,
  output S_3,
  output Cout_3,
  output S_4,
  output Cout_4,
  output S_5,
  output Cout_5,
  output S_6,
  output Cout_6,
  output S_7,
  output Cout_7,
  output S_8,
  output Cout_8
);

  wire and_1_out, and_2_out, and_4_out, and_5_out, and_6_out, nand_1_out, nand_2_out, not_1_out, not_2_out,
       not_3_out, not_4_out, not_5_out, not_6_out, not_8_out, not_9_out, xor_1_out, xor_4_out, xor_6_out;

  xor xor_1 (xor_1_out, A, B);
  and and_1 (and_1_out, A, B);
  xor xor_2 (S, xor_1_out, Cin);
  and and_2 (and_2_out, xor_1_out, Cin);
  or or_1 (Cout, and_2_out, and_1_out);
  xor xor_3 (S_2, A_2, B_2);
  and and_3 (Cout_2, A_2, B_2);
  not not_1 (not_1_out, B_3);
  xor xor_4 (xor_4_out, A_3, not_1_out);
  and and_4 (and_4_out, A_3, not_1_out);
  xor xor_5 (S_3, xor_4_out, Cin_2);
  and and_5 (and_5_out, xor_4_out, Cin_2);
  or or_2 (Cout_3, and_5_out, and_4_out);
  not not_2 (not_2_out, B_4);
  not not_3 (not_3_out, B_5);
  not not_4 (not_4_out, B_6);
  xor xor_6 (xor_6_out, A_4, not_2_out);
  and and_6 (and_6_out, A_4, not_2_out);
  xnor xnor_1 (S_5, A_5, not_3_out);
  nand nand_1 (nand_1_out, A_5, not_3_out);
  xnor xnor_2 (S_6, A_6, not_4_out);
  nand nand_2 (nand_2_out, A_6, not_4_out);
  xor xor_7 (S_7, A_7, B_7);
  not not_5 (not_5_out, A_7);
  nand nand_3 (Cout_7, not_5_out, B_7);
  xor xor_8 (S_8, A_8, B_8);
  not not_6 (not_6_out, B_8);
  or or_3 (Cout_8, A_8, not_6_out);
  not not_7 (S_4, xor_6_out);
  or or_4 (Cout_4, xor_6_out, and_6_out);
  not not_8 (not_8_out, S_5);
  not not_9 (not_9_out, nand_1_out);
  nand nand_4 (Cout_6, S_6, nand_2_out);
  or or_5 (Cout_5, not_8_out, not_9_out);
endmodule
